# Fritzing sketch blink-circuit (saved by Fritzing 0.9.1b)
circuit board: 5.28706cm x 3.23899cm
breadboards: 1

parts:
  Arduino_Micro = Arduino Micro (Rev3)
  JP1 = Header 2 [package=molex-1x2_lock]
  R1 = Resistor [tolerance=±5% resistance=1k package=THT]
  LED1 = LED - 5mm [color="Red (633nm)" package="5 mm [THT]"]

nets:
  N1: Arduino_Micro.GND, JP1.1, LED1.cathode
  N2: Arduino_Micro.VIN, JP1.2
  N3: Arduino_Micro.D13_PWM, R1.Pin_1
  N4: R1.Pin_0, LED1.anode
