# Fritzing sketch colors-circuit (saved by Fritzing 0.9.1b)
circuit board: 5.17173cm x 3.86644cm
breadboards: 1

parts:
  Arduino_Micro = Arduino Micro (Rev3)
  R1 = Resistor [tolerance=±5% resistance=1k package=THT]
  R2 = Resistor [tolerance=±5% resistance=3.3k package=THT]
  R3 = Resistor [tolerance=±5% resistance=3.3k package=THT]
  R4 = Resistor [tolerance=±5% resistance=3.3k package=THT]
  JP2 = Header 2 [package=molex-1x2_lock]
  C1 = Ceramic Capacitor [capacitance=0.1µF package="100 mil [THT, multilayer]"]
  LED1 = RGB LED (com. cathode, rgb) [package="5 mm [THT]"]
  C2 = Ceramic Capacitor [capacitance=0.1µF package="100 mil [THT, multilayer]"]
  C3 = Ceramic Capacitor [capacitance=0.1µF package="100 mil [THT, multilayer]"]

nets:
  N1: Arduino_Micro.GND, JP2.2, C1.0, C2.1, C3.1
  N2: Arduino_Micro.D3/SCL, R4.Pin_0
  N3: Arduino_Micro.D5_PWM, R3.Pin_0
  N4: Arduino_Micro.D6_PWM/A7, R2.Pin_0
  N5: Arduino_Micro.VIN, JP2.1
  N6: Arduino_Micro.5V, R1.Pin_0
  N7: R1.Pin_1, LED1.common_cathode
  N8: R2.Pin_1, C1.1, LED1.red_anode
  N9: R3.Pin_1, LED1.green_anode, C2.0
  N10: R4.Pin_1, LED1.blue_anode, C3.0
