# Fritzing sketch dotstar_circuit (saved by Fritzing 0.9.1b)
circuit board: 6.36882cm x 3.73474cm
breadboards: 1

parts:
  Arduino_Micro = Arduino Micro (Rev3)
  5V_GND = Header 2 [package=molex-1x2_lock]
  C1 = Capacitor Polarized [package=cpol-radial-1000uf-25v]
  7-12V_GND = Header 2 [package=molex-1x2_lock]
  GND_Dat_Clk_+5 = Header 4 [package=molex-1x4_lock]
  R1 = Resistor [tolerance=±5% resistance=3.3k package=THT]

nets:
  N1: Arduino_Micro.D3/SCL, GND_Dat_Clk_+5.3
  N2: Arduino_Micro.D4_PWM/A6, R1.Pin_0
  N3: Arduino_Micro.VIN, 7-12V_GND.1
  N4: Arduino_Micro.GND, 5V_GND.2, C1.-, 7-12V_GND.2, GND_Dat_Clk_+5.1
  N5: 5V_GND.1, C1.+, GND_Dat_Clk_+5.4
  N6: GND_Dat_Clk_+5.2, R1.Pin_1
